// Digital circuit ULA.dig as structural Verilog
module ULA (
  input  [31:0] A,
  input  [31:0] B,
  input  [3:0] Op,
  output Zero,
  output [31:0] Result
);

  ULA #(.applicationType("IVERILOG")) u_ULA (
    .operand1(A), .operand2(B), .ALU_control_vector(Op), .ALU_result(Result), .zero(Zero));
endmodule

/* Test case ULA:
A B Op Y
 loop(i,5)
   let a = random(1<<8);
   let b = random(1<<8);
   (a) (b) 0 (a & b)
   (a) (b) 1 (a | b)
   (a) (b) 2 (a + b)
   (a) (b) 3 (a - b)
 end loop
*/

/* Code of ULA:
module ULA(
	input [31:0] operand1, operand2,
	input [3:0] ALU_control_vector,
	output [31:0] ALU_result,
	output reg zero
);

	reg [31:0] ALU_result;

	always @(*) begin
           case (ALU_control_vector)
              0: ALU_result = operand1 & operand2;
              1: ALU_result = operand1 | operand2;
              2: ALU_result = operand1 + operand2;
              6: ALU_result = operand1 - operand2;
	      7: ALU_result = operand1 < operand2;
              12: ALU_result = ~(operand1 | operand2);
	      default: ALU_result = 32'd0;
	   endcase
	   if(ALU_result == 32'd0)begin
           	zero = 1'b1;
           end else begin
	   	zero = 1'b0;
           end
        end

endmodule
*/
